# Fritzing sketch Miller (saved by Fritzing 0.9.3b)
breadboards: 1

parts:
  Componente1 = Arduino Mega 2560 (Rev3)
  MOTOR_DRIVER = H-Bridge with L298N
  MPU9250 = GY-5150 (MPU-9150) [form="♀ (female)" package=THT]
  LEFT_SONAR = hc-sr04
  RIGHT_SONAR = hc-sr04
  YwRobot_Power_Supply1 = YwRobot Breadboard Power Supply [part_number=545043]
  RIGHT_WHEEL = DC Motor
  LEFT_WHEEL = DC Motor  # not connected
  VCC1 = Battery block 9V
  LEFT_IR = fc-51 [package=THT]
  RIGHT_IR = fc-51 [package=THT]
  FRONT_IR = fc-51 [package=THT]
  J1 = Basic Servo
  part = ESP8266 WiFi Module [part_number=ESP8266]
  UP_IR = fc-51 [package=THT]
  ARM_LEFT_IR = fc-51 [package=THT]
  ARM_FRONT_IR = fc-51 [package=THT]
  ARM_RIGHT_IR = fc-51 [package=THT]

nets:
  N1: Componente1.A15, ARM_RIGHT_IR.pin1
  N2: Componente1.A1, RIGHT_SONAR.Trig
  N3: Componente1.A2, RIGHT_SONAR.Echo
  N4: Componente1.A7, UP_IR.pin1
  N5: Componente1.D21/SCL, MPU9250.pin3
  N6: Componente1.D20/SDA, MPU9250.pin4
  N7: Componente1.D19/RX1, part.TXD
  N8: Componente1.D18/TX1, part.RXD
  GND: Componente1.GND, Componente1.VIN, VCC1.-
  N9: Componente1.D11_PWM, J1.pulse
  N10: Componente1.D10_PWM, LEFT_SONAR.Echo
  N11: Componente1.D9_PWM, LEFT_SONAR.Trig
  3V3: Componente1.3V3, part.VCC, part.CH_PD
  N12: Componente1.D2_PWM, MPU9250.pin8
  N13: Componente1.D4_PWM, MOTOR_DRIVER.IN2
  N14: Componente1.D5_PWM, MOTOR_DRIVER.IN1
  N15: Componente1.D6_PWM, MOTOR_DRIVER.IN4
  N16: Componente1.D7_PWM, MOTOR_DRIVER.IN3
  N17: Componente1.D22, FRONT_IR.pin1
  N18: Componente1.D36, LEFT_IR.pin1
  N19: Componente1.D38, ARM_FRONT_IR.pin1
  N20: Componente1.D40, RIGHT_IR.pin1
  N21: MOTOR_DRIVER.12V, VCC1.+
  N22: MOTOR_DRIVER.OUT4-Motor2, RIGHT_WHEEL.pin_1
  N23: MPU9250.pin1, RIGHT_SONAR.VCC, YwRobot_Power_Supply1.VCC#9, YwRobot_Power_Supply1.VCC#10, RIGHT_IR.pin3, UP_IR.pin3, ARM_RIGHT_IR.pin2, ARM_RIGHT_IR.pin3
  N24: MPU9250.pin2, RIGHT_SONAR.GND, YwRobot_Power_Supply1.GND#13, YwRobot_Power_Supply1.GND#14, RIGHT_IR.pin2, UP_IR.pin2
  VCC: LEFT_SONAR.VCC, YwRobot_Power_Supply1.VCC#5, YwRobot_Power_Supply1.VCC#6, LEFT_IR.pin3, FRONT_IR.pin3, J1.vcc, ARM_LEFT_IR.pin3, ARM_FRONT_IR.pin3
  GND_2: LEFT_SONAR.GND, YwRobot_Power_Supply1.GND#11, YwRobot_Power_Supply1.GND#12, LEFT_IR.pin2, FRONT_IR.pin2, J1.gnd, ARM_LEFT_IR.pin2, ARM_FRONT_IR.pin2

custom parts:
  H-Bridge with L298N: h-bridge
  GY-5150 (MPU-9150): Placa GY-5150 basada en conjunto de acelerómetro+giroscopios+magnetómetro MPU-9150
  YwRobot Breadboard Power Supply: The YwRobot Breadboard Power Supply (MB-V2) has two power rails; they can be 5V or 3V3. Power to the module can be provided through the female USB socket or through the A10 (female) 2.1mm power jack.
  ESP8266 WiFi Module: Generic WiFi Module based on the ESP8266 with onboard PCB antenna and UART communications
